// Logisim project comp_2.circ as structural Verilog: 4 circuits, main circuit add_1
module add_1 (
  input  a,
  input  b,
  input  vem_1,
  output s,
  output vai_1
);

  wire and_1_out, and_2_out, or_1_out, xor_1_out;

  xor xor_1 (xor_1_out, b, a);
  or or_1 (or_1_out, vem_1, b);
  and and_1 (and_1_out, b, vem_1);
  xor xor_2 (s, vem_1, xor_1_out);
  and and_2 (and_2_out, or_1_out, a);
  or or_2 (vai_1, and_2_out, and_1_out);
endmodule

module add_4 (
  input  [3:0] in_1,
  input  [3:0] in_2,
  output overflow,
  output [3:0] out_4
);

  wire add_1_1_vai_1, add_1_3_vai_1, add_1_4_vai_1;

  add_1 add_1_1 (.s(out_4[2]), .vai_1(add_1_1_vai_1), .a(in_2[2]), .b(in_1[2]), .vem_1(add_1_3_vai_1));
  add_1 add_1_2 (.s(out_4[3]), .vai_1(overflow), .a(in_2[3]), .b(in_1[3]), .vem_1(add_1_1_vai_1));
  add_1 add_1_3 (.s(out_4[1]), .vai_1(add_1_3_vai_1), .a(in_2[1]), .b(in_1[1]), .vem_1(add_1_4_vai_1));
  add_1 add_1_4 (.s(out_4[0]), .vai_1(add_1_4_vai_1), .a(in_2[0]), .b(in_1[0]), .vem_1(1'b0));
endmodule

module comp_2 (
  input  [3:0] in_1,
  output [3:0] out_2
);

  wire [3:0] not_3_out;

  not not_1 (not_3_out[2], in_1[2]);
  not not_2 (not_3_out[3], in_1[3]);
  not not_3 (not_3_out[0], in_1[0]);
  not not_4 (not_3_out[1], in_1[1]);
  add_4 add_4_1 (.in_2(not_3_out), .in_1(4'b0001), .out_4(out_2));  // open: overflow
endmodule

module sub (
  input  [3:0] in_1,
  input  [3:0] in_2,
  output [3:0] out_3
);

  wire [3:0] comp_2_1_out_2;

  comp_2 comp_2_1 (.in_1(in_2), .out_2(comp_2_1_out_2));
  add_4 add_4_1 (.in_2(in_1), .in_1(comp_2_1_out_2), .out_4(out_3));  // open: overflow
endmodule
