// Logisim project numerodigital.circ as structural Verilog: 2 circuits, main circuit main
module main (
  input  a,
  input  b,
  input  c,
  input  d,
  output a_2,
  output b_2,
  output c_2,
  output d_2,
  output e,
  output f,
  output g
);

  wire and_1_out, and_2_out, and_3_out, and_4_out, and_5_out, and_6_out, and_7_out, and_8_out, and_9_out,
       and_10_out, and_11_out, and_12_out, xnor_1_out, xnor_2_out;

  xnor xnor_1 (xnor_1_out, b, d);
  xnor xnor_2 (xnor_2_out, c, d);
  or or_1 (c_2, b, ~c, d);  // OR_Gate
  and and_1 (and_1_out, ~b, ~d);  // AND_Gate
  and and_2 (and_2_out, ~b, c);  // AND_Gate
  and and_3 (and_3_out, c, ~d);  // AND_Gate
  and and_4 (and_4_out, b, ~c, d);  // AND_Gate
  and and_5 (and_5_out, ~b, ~d);  // AND_Gate
  and and_6 (and_6_out, c, ~d);  // AND_Gate
  and and_7 (and_7_out, ~c, ~d);  // AND_Gate
  and and_8 (and_8_out, b, ~c);  // AND_Gate
  and and_9 (and_9_out, b, ~d);  // AND_Gate
  and and_10 (and_10_out, b, ~c);  // AND_Gate
  and and_11 (and_11_out, ~b, c);  // AND_Gate
  and and_12 (and_12_out, c, ~d);  // AND_Gate
  or or_2 (b_2, xnor_2_out, ~b);  // OR_Gate
  or or_3 (a_2, xnor_1_out, a, c);
  or or_4 (d_2, a, and_1_out, and_2_out, and_3_out, and_4_out);
  or or_5 (e, and_5_out, and_6_out);
  or or_6 (f, a, and_7_out, and_8_out, and_9_out);
  or or_7 (g, a, and_10_out, and_11_out, and_12_out);
endmodule

module numero (
  input  [3:0] in_1
);

  wire main_1_a_2, main_1_b_2, main_1_c_2, main_1_d_2, main_1_e, main_1_f, main_1_g;

  main main_1 (
    .a(in_1[3]), .b(in_1[2]), .c(in_1[1]), .d(in_1[0]), .a_2(main_1_a_2), .b_2(main_1_b_2), .c_2(main_1_c_2),
    .d_2(main_1_d_2), .e(main_1_e), .f(main_1_f), .g(main_1_g));
  _7_Segment_Display u_7_segment_display_1 (
    .g(main_1_g), .f(main_1_f), .a(main_1_a_2), .b(main_1_b_2), .e(main_1_e), .d(main_1_d_2), .c(main_1_c_2));  // open: dp
endmodule
