// Logisim project paridade.circ as structural Verilog: 2 circuits, main circuit main
module main (
  input  a,
  input  b,
  input  c,
  input  d,
  output out_5
);

  wire xor_1_out, xor_2_out;

  xor xor_1 (xor_1_out, a, b);
  xor xor_2 (xor_2_out, c, d);
  xor xor_3 (out_5, xor_1_out, xor_2_out);
endmodule

module paridade (
  input  [3:0] in_1,
  output out_2
);

  main main_1 (.out_5(out_2), .a(in_1[0]), .b(in_1[1]), .c(in_1[2]), .d(in_1[3]));
endmodule
