// Logisim project projeto_contador.circ as structural Verilog: 1 circuit, main circuit main
module main (
);

  wire clock_1_out, j_k_ff_1_qn, j_k_ff_2_qn;
  wire [2:0] j_k_ff_3_q;

  Clock clock_1 (.out(clock_1_out));
  J_K_Flip_Flop j_k_ff_1 (
    .J(j_k_ff_3_q[1]), .clk(clock_1_out), .K(j_k_ff_2_qn), .Q(j_k_ff_3_q[2]), .Qn(j_k_ff_1_qn));  // open: preset, en, reset
  J_K_Flip_Flop j_k_ff_2 (
    .J(j_k_ff_1_qn), .clk(clock_1_out), .K(j_k_ff_3_q[2]), .Q(j_k_ff_3_q[1]), .Qn(j_k_ff_2_qn));  // open: preset, en, reset
  // Probe on j_k_ff_3_q
  J_K_Flip_Flop j_k_ff_3 (
    .J(1'b1), .clk(clock_1_out), .K(j_k_ff_2_qn), .Q(j_k_ff_3_q[0]));  // open: Qn, preset, en, reset
endmodule
